// Logisim project EL2-8_4IT - Memoria RAM.circ as structural Verilog: 3 circuits, main circuit circuito1
module circuito1 (
  input  [7:0] Data_0,
  input  [7:0] Data_1
);

  wire ADDR0, ADDR1, ADDR2, ADDR3, ADDR4, ADDR5, ADDR6, ADDR7, and_2_out, and_3_out, and_4_out, and_5_out,
       clock_1_out, DIP0, DIP1, DIP2, DIP3, ENTER, IOREAD, IOREQ, IOWRITE, MREQ, MRQRD, nor_3_out, or_2_out,
       or_3_out, or_4_out, or_5_out, RD, RESET, RUN, t_ff_1_q, t_ff_2_q, WAIT, WAIT0, WAIT1, WR;
  wire [1:0] UP_out;
  wire [3:0] OUT00_3, OUT04_7, OUT10_3, OUT14_7;
  wire [7:0] ADDR, controlled_buffer_4_out, controlled_buffer_6_out, DATA_IN, DATA_OUT, ram_1_data,
       rom_1_data;

  // DipSwitch Porta_input_4: pin names not known; wires that end beside it: DIP3, DIP2, DIP1, DIP0
  Hex_Digit_Display hex_digit_display_1 (.value(OUT14_7));  // open: dp
  Hex_Digit_Display hex_digit_display_2 (.value(OUT10_3));  // open: dp
  or or_1 (MRQRD, MREQ, RD);
  Decoder #(.select(3), .enable("false")) decoder_1 (
    .out0(ADDR0), .out1(ADDR1), .out2(ADDR2), .out3(ADDR3), .out4(ADDR4), .out5(ADDR5), .out6(ADDR6),
    .out7(ADDR7), .sel(ADDR[2:0]));
  Button Porta_Input_3 (.out(RUN));
  Button u_Enter (.out(ENTER));
  Button u_Reset (.out(RESET));
  // Probe on Data_0
  // Probe on Data_1
  Hex_Digit_Display hex_digit_display_3 (.value(OUT04_7));  // open: dp
  nor nor_1 (IOREAD, RD, IOREQ);
  and and_1 (WAIT, WAIT0, WAIT1);
  nor nor_2 (IOWRITE, WR, IOREQ);
  Hex_Digit_Display hex_digit_display_4 (.value(OUT00_3));  // open: dp
  Clock clock_1 (.out(clock_1_out));
  or or_2 (or_2_out, MREQ, ADDR[7]);
  assign DATA_IN = and_2_out ? Data_0 : 8'bz;  // Controlled_Buffer controlled_buffer_1
  and and_2 (and_2_out, IOREAD, ADDR0);
  assign DATA_IN = and_3_out ? Data_1 : 8'bz;  // Controlled_Buffer controlled_buffer_2
  and and_3 (and_3_out, IOREAD, ADDR1);
  ROM #(.addrWidth(7), .Select("low")) rom_1 (.addr(ADDR[6:0]), .data(rom_1_data), .sel(or_2_out));
  // ß2018 ß2018_1: pin names not known; wires that end beside it: DATA_IN, clock_1_out, WAIT, RESET, ADDR, MREQ, RD, IOREQ, WR, DATA_OUT
  T_Flip_Flop t_ff_1 (.clk(and_2_out), .T(1'b1), .Q(t_ff_1_q), .Qn(WAIT0), .reset(ENTER));  // open: preset
  T_Flip_Flop t_ff_2 (.clk(and_3_out), .T(1'b1), .Q(t_ff_2_q), .Qn(WAIT1), .reset(ENTER));  // open: preset
  assign DATA_IN = ~or_3_out ? rom_1_data : 8'bz;  // Controlled_Buffer controlled_buffer_3
  or or_3 (or_3_out, MREQ, RD);
  LED led_1 (.in(t_ff_1_q));
  LED led_2 (.in(t_ff_2_q));
  and and_4 (and_4_out, IOREAD, ADDR2);
  assign controlled_buffer_4_out = ADDR0 ? DATA_OUT : 8'bz;  // Controlled_Buffer controlled_buffer_4
  or or_4 (or_4_out, MREQ, ~ADDR[7]);  // OR_Gate
  assign DATA_IN = and_4_out ? {{6{1'b0}}, UP_out} : 8'bz;  // Controlled_Buffer controlled_buffer_5
  assign controlled_buffer_6_out = ADDR1 ? DATA_OUT : 8'bz;  // Controlled_Buffer controlled_buffer_6
  Button UP (.out(UP_out[0]));
  Button DOWN (.out(UP_out[1]));
  Register #(.Select("high")) register_1 (
    .D(controlled_buffer_4_out), .Q({OUT04_7, OUT00_3}), .clk(IOWRITE), .clr(RESET));  // open: en
  Register #(.Select("high")) register_2 (
    .D(controlled_buffer_6_out), .Q({OUT14_7, OUT10_3}), .clk(IOWRITE), .clr(RESET));  // open: en
  RAM #(.addrWidth(7), .bus("separate"), .Select("low")) ram_1 (
    .addr(ADDR[6:0]), .din(DATA_OUT), .data(ram_1_data), .sel(or_4_out), .clk(nor_3_out));  // open: str, ld, clr
  nor nor_3 (nor_3_out, WR, MREQ);
  assign DATA_IN = ~or_5_out ? ram_1_data : 8'bz;  // Controlled_Buffer controlled_buffer_7
  or or_5 (or_5_out, MREQ, RD);
  and and_5 (and_5_out, IOREAD, ADDR3);
  assign DATA_IN = and_5_out ? {4'b0000, DIP3, DIP2, DIP1, DIP0} : 8'bz;  // Controlled_Buffer controlled_buffer_8

  // Other names for the same wires on the sheet: ADDR06[6:0] = ADDR[6:0]; ADDR07 = ADDR[7]

  // Notes on the sheet:
  //   Porta OUT 1
  //   Porta OUT 0
  //   contents of rom_1 (hex, n*v repeats v):
  //   e 80 3e 0 77 c 3c fe 7f c2 4 76
endmodule

module circuito2 (
  input  [7:0] Data_0,
  input  [7:0] Data_1
);

  wire ADDR0, ADDR1, ADDR2, ADDR3, ADDR4, ADDR5, ADDR6, ADDR7, and_2_out, and_3_out, and_4_out, and_5_out,
       clock_1_out, DIP0, DIP1, DIP2, DIP3, ENTER, IOREAD, IOREQ, IOWRITE, MREQ, MRQRD, nor_3_out, or_2_out,
       or_3_out, or_4_out, or_5_out, RD, RESET, RUN, t_ff_1_q, t_ff_2_q, WAIT, WAIT0, WAIT1, WR;
  wire [1:0] UP_out;
  wire [3:0] OUT00_3, OUT04_7, OUT10_3, OUT14_7;
  wire [7:0] ADDR, controlled_buffer_4_out, controlled_buffer_6_out, DATA_IN, DATA_OUT, ram_1_data,
       rom_1_data;

  // DipSwitch Porta_input_4: pin names not known; wires that end beside it: DIP3, DIP2, DIP1, DIP0
  Hex_Digit_Display hex_digit_display_1 (.value(OUT14_7));  // open: dp
  Hex_Digit_Display hex_digit_display_2 (.value(OUT10_3));  // open: dp
  or or_1 (MRQRD, MREQ, RD);
  Decoder #(.select(3), .enable("false")) decoder_1 (
    .out0(ADDR0), .out1(ADDR1), .out2(ADDR2), .out3(ADDR3), .out4(ADDR4), .out5(ADDR5), .out6(ADDR6),
    .out7(ADDR7), .sel(ADDR[2:0]));
  Button Porta_Input_3 (.out(RUN));
  Button u_Enter (.out(ENTER));
  Button u_Reset (.out(RESET));
  // Probe on Data_0
  // Probe on Data_1
  Hex_Digit_Display hex_digit_display_3 (.value(OUT04_7));  // open: dp
  nor nor_1 (IOREAD, RD, IOREQ);
  and and_1 (WAIT, WAIT0, WAIT1);
  nor nor_2 (IOWRITE, WR, IOREQ);
  Hex_Digit_Display hex_digit_display_4 (.value(OUT00_3));  // open: dp
  Clock clock_1 (.out(clock_1_out));
  or or_2 (or_2_out, MREQ, ADDR[7]);
  assign DATA_IN = and_2_out ? Data_0 : 8'bz;  // Controlled_Buffer controlled_buffer_1
  and and_2 (and_2_out, IOREAD, ADDR0);
  assign DATA_IN = and_3_out ? Data_1 : 8'bz;  // Controlled_Buffer controlled_buffer_2
  and and_3 (and_3_out, IOREAD, ADDR1);
  ROM #(.addrWidth(7), .Select("low")) rom_1 (.addr(ADDR[6:0]), .data(rom_1_data), .sel(or_2_out));
  // ß2018 ß2018_1: pin names not known; wires that end beside it: DATA_IN, clock_1_out, WAIT, RESET, ADDR, MREQ, RD, IOREQ, WR, DATA_OUT
  T_Flip_Flop t_ff_1 (.clk(and_2_out), .T(1'b1), .Q(t_ff_1_q), .Qn(WAIT0), .reset(ENTER));  // open: preset
  T_Flip_Flop t_ff_2 (.clk(and_3_out), .T(1'b1), .Q(t_ff_2_q), .Qn(WAIT1), .reset(ENTER));  // open: preset
  assign DATA_IN = ~or_3_out ? rom_1_data : 8'bz;  // Controlled_Buffer controlled_buffer_3
  or or_3 (or_3_out, MREQ, RD);
  LED led_1 (.in(t_ff_1_q));
  LED led_2 (.in(t_ff_2_q));
  and and_4 (and_4_out, IOREAD, ADDR2);
  assign controlled_buffer_4_out = ADDR0 ? DATA_OUT : 8'bz;  // Controlled_Buffer controlled_buffer_4
  or or_4 (or_4_out, MREQ, ~ADDR[7]);  // OR_Gate
  assign DATA_IN = and_4_out ? {{6{1'b0}}, UP_out} : 8'bz;  // Controlled_Buffer controlled_buffer_5
  assign controlled_buffer_6_out = ADDR1 ? DATA_OUT : 8'bz;  // Controlled_Buffer controlled_buffer_6
  Button UP (.out(UP_out[0]));
  Button DOWN (.out(UP_out[1]));
  Register #(.Select("high")) register_1 (
    .D(controlled_buffer_4_out), .Q({OUT04_7, OUT00_3}), .clk(IOWRITE), .clr(RESET));  // open: en
  Register #(.Select("high")) register_2 (
    .D(controlled_buffer_6_out), .Q({OUT14_7, OUT10_3}), .clk(IOWRITE), .clr(RESET));  // open: en
  RAM #(.addrWidth(7), .bus("separate"), .Select("low")) ram_1 (
    .addr(ADDR[6:0]), .din(DATA_OUT), .data(ram_1_data), .sel(or_4_out), .clk(nor_3_out));  // open: str, ld, clr
  nor nor_3 (nor_3_out, WR, MREQ);
  assign DATA_IN = ~or_5_out ? ram_1_data : 8'bz;  // Controlled_Buffer controlled_buffer_7
  or or_5 (or_5_out, MREQ, RD);
  and and_5 (and_5_out, IOREAD, ADDR3);
  assign DATA_IN = and_5_out ? {4'b0000, DIP3, DIP2, DIP1, DIP0} : 8'bz;  // Controlled_Buffer controlled_buffer_8

  // Other names for the same wires on the sheet: ADDR06[6:0] = ADDR[6:0]; ADDR07 = ADDR[7]

  // Notes on the sheet:
  //   Porta OUT 1
  //   Porta OUT 0
  //   contents of rom_1 (hex, n*v repeats v):
  //   6 80 48 3e 0 77 7e fe 0 c2 1a 3e ff 77 7e fe ff c2 1a 4 48 fe 0 c2 3 76 78 d3 0 76
endmodule

module circuito3 (
  input  [7:0] Data_0,
  input  [7:0] Data_1
);

  wire ADDR0, ADDR1, ADDR2, ADDR3, ADDR4, ADDR5, ADDR6, ADDR7, and_2_out, and_3_out, and_4_out, and_5_out,
       clock_1_out, DIP0, DIP1, DIP2, DIP3, ENTER, IOREAD, IOREQ, IOWRITE, MREQ, MRQRD, nor_3_out, or_2_out,
       or_3_out, or_4_out, or_5_out, RD, RESET, RUN, t_ff_1_q, t_ff_2_q, WAIT, WAIT0, WAIT1, WR;
  wire [1:0] UP_out;
  wire [3:0] OUT00_3, OUT04_7, OUT10_3, OUT14_7;
  wire [7:0] ADDR, controlled_buffer_4_out, controlled_buffer_6_out, DATA_IN, DATA_OUT, ram_1_data,
       rom_1_data;

  // DipSwitch Porta_input_4: pin names not known; wires that end beside it: DIP3, DIP2, DIP1, DIP0
  Hex_Digit_Display hex_digit_display_1 (.value(OUT14_7));  // open: dp
  Hex_Digit_Display hex_digit_display_2 (.value(OUT10_3));  // open: dp
  or or_1 (MRQRD, MREQ, RD);
  Decoder #(.select(3), .enable("false")) decoder_1 (
    .out0(ADDR0), .out1(ADDR1), .out2(ADDR2), .out3(ADDR3), .out4(ADDR4), .out5(ADDR5), .out6(ADDR6),
    .out7(ADDR7), .sel(ADDR[2:0]));
  Button Porta_Input_3 (.out(RUN));
  Button u_Enter (.out(ENTER));
  Button u_Reset (.out(RESET));
  // Probe on Data_0
  // Probe on Data_1
  Hex_Digit_Display hex_digit_display_3 (.value(OUT04_7));  // open: dp
  nor nor_1 (IOREAD, RD, IOREQ);
  and and_1 (WAIT, WAIT0, WAIT1);
  nor nor_2 (IOWRITE, WR, IOREQ);
  Hex_Digit_Display hex_digit_display_4 (.value(OUT00_3));  // open: dp
  Clock clock_1 (.out(clock_1_out));
  or or_2 (or_2_out, MREQ, ADDR[7]);
  assign DATA_IN = and_2_out ? Data_0 : 8'bz;  // Controlled_Buffer controlled_buffer_1
  and and_2 (and_2_out, IOREAD, ADDR0);
  assign DATA_IN = and_3_out ? Data_1 : 8'bz;  // Controlled_Buffer controlled_buffer_2
  and and_3 (and_3_out, IOREAD, ADDR1);
  ROM #(.addrWidth(7), .Select("low")) rom_1 (.addr(ADDR[6:0]), .data(rom_1_data), .sel(or_2_out));
  // ß2018 ß2018_1: pin names not known; wires that end beside it: DATA_IN, clock_1_out, WAIT, RESET, ADDR, MREQ, RD, IOREQ, WR, DATA_OUT
  T_Flip_Flop t_ff_1 (.clk(and_2_out), .T(1'b1), .Q(t_ff_1_q), .Qn(WAIT0), .reset(ENTER));  // open: preset
  T_Flip_Flop t_ff_2 (.clk(and_3_out), .T(1'b1), .Q(t_ff_2_q), .Qn(WAIT1), .reset(ENTER));  // open: preset
  assign DATA_IN = ~or_3_out ? rom_1_data : 8'bz;  // Controlled_Buffer controlled_buffer_3
  or or_3 (or_3_out, MREQ, RD);
  LED led_1 (.in(t_ff_1_q));
  LED led_2 (.in(t_ff_2_q));
  and and_4 (and_4_out, IOREAD, ADDR2);
  assign controlled_buffer_4_out = ADDR0 ? DATA_OUT : 8'bz;  // Controlled_Buffer controlled_buffer_4
  or or_4 (or_4_out, MREQ, ~ADDR[7]);  // OR_Gate
  assign DATA_IN = and_4_out ? {{6{1'b0}}, UP_out} : 8'bz;  // Controlled_Buffer controlled_buffer_5
  assign controlled_buffer_6_out = ADDR1 ? DATA_OUT : 8'bz;  // Controlled_Buffer controlled_buffer_6
  Button UP (.out(UP_out[0]));
  Button DOWN (.out(UP_out[1]));
  Register #(.Select("high")) register_1 (
    .D(controlled_buffer_4_out), .Q({OUT04_7, OUT00_3}), .clk(IOWRITE), .clr(RESET));  // open: en
  Register #(.Select("high")) register_2 (
    .D(controlled_buffer_6_out), .Q({OUT14_7, OUT10_3}), .clk(IOWRITE), .clr(RESET));  // open: en
  RAM #(.addrWidth(7), .bus("separate"), .Select("low")) ram_1 (
    .addr(ADDR[6:0]), .din(DATA_OUT), .data(ram_1_data), .sel(or_4_out), .clk(nor_3_out));  // open: str, ld, clr
  nor nor_3 (nor_3_out, WR, MREQ);
  assign DATA_IN = ~or_5_out ? ram_1_data : 8'bz;  // Controlled_Buffer controlled_buffer_7
  or or_5 (or_5_out, MREQ, RD);
  and and_5 (and_5_out, IOREAD, ADDR3);
  assign DATA_IN = and_5_out ? {4'b0000, DIP3, DIP2, DIP1, DIP0} : 8'bz;  // Controlled_Buffer controlled_buffer_8

  // Other names for the same wires on the sheet: ADDR06[6:0] = ADDR[6:0]; ADDR07 = ADDR[7]

  // Notes on the sheet:
  //   Porta OUT 1
  //   Porta OUT 0
  //   contents of rom_1 (hex, n*v repeats v):
  //   3e b 32 80 e 81 3a 80 ee ff c6 49 ee ff 32 80 77 c fe ff ca 18 c2 6 76
endmodule
