// Logisim project Tris.circ as structural Verilog: 8 circuits, main circuit test_primo
module test_primo (
);

  wire b1, b2, b3, b4, b5, b6, b7, b8, b9, clock_1_out, r1, r2, r3, r4, r5, r6, r7, r8, r9;
  wire [7:0] counter_1_q, rom_1_data;

  Counter #(.max('h8)) counter_1 (
    .Q(counter_1_q), .clk(clock_1_out));  // open: load, D, count, carry, clr, preset, down
  Clock clock_1 (.out(clock_1_out));
  ROM #(.Select("low")) rom_1 (.addr(counter_1_q), .data(rom_1_data));
  Demultiplexer #(.select(4), .width(2), .enable("false")) demultiplexer_1 (
    .out0({b1, r1}), .out1({b2, r2}), .out2({b3, r3}), .out3({b4, r4}), .out4({b5, r5}), .out5({b6, r6}),
    .out6({b7, r7}), .out7({b8, r8}), .out8({b9, r9}), .in(rom_1_data[1:0]), .sel(counter_1_q[3:0]));  // open: out9, out10, out11, out12, out13, out14, out15
  // RGBLed rgbled_1: pin names not known; wires that end beside it: r1, b1
  // RGBLed rgbled_2: pin names not known; wires that end beside it: r4, b4
  // RGBLed rgbled_3: pin names not known; wires that end beside it: r7, b7
  // RGBLed rgbled_4: pin names not known; wires that end beside it: r2, b2
  // RGBLed rgbled_5: pin names not known; wires that end beside it: r3, b3
  // RGBLed rgbled_6: pin names not known; wires that end beside it: r5, b5
  // RGBLed rgbled_7: pin names not known; wires that end beside it: r6, b6
  // RGBLed rgbled_8: pin names not known; wires that end beside it: r8, b8
  // RGBLed rgbled_9: pin names not known; wires that end beside it: r9, b9

  // Notes on the sheet:
  //   contents of rom_1 (hex, n*v repeats v):
  //   1 2 2 1 3 1 2 2 3
endmodule

module test_casino (
  output out_1
);

  wire _1, _2, _3, _4, _5, _6, _7, _8, _9, and_1_out, b1, b2, b3, b4, b5, b6, b7, b8, b9, clk, CONFIRM_out,
       r1, r2, r3, r4, r5, r6, r7, r8, r9;
  wire [1:0] adder_1_out, counter_1_q, demultiplexer_1_out0, demultiplexer_1_out1, demultiplexer_1_out2,
       demultiplexer_1_out3, demultiplexer_1_out4, demultiplexer_1_out5, demultiplexer_1_out6,
       demultiplexer_1_out7, demultiplexer_1_out8, not_1_out, ram_1_data;
  wire [3:0] counter_2_q;

  // RGBLed rgbled_1: pin names not known; wires that end beside it: r1, _1, b1
  // RGBLed rgbled_2: pin names not known; wires that end beside it: r4, _4, b4
  // RGBLed rgbled_3: pin names not known; wires that end beside it: r7, _7, b7
  Counter #(.width(2), .max('h1)) counter_1 (
    .Q(counter_1_q), .clk(and_1_out));  // open: load, D, count, carry, clr, preset, down
  and and_1 (and_1_out, out_1, CONFIRM_out);
  Button CONFIRM (.out(CONFIRM_out));
  Adder #(.width(2)) adder_1 (.a(2'b01), .b(counter_1_q), .out(adder_1_out));  // open: cin, cout
  // RGBLed rgbled_4: pin names not known; wires that end beside it: r2, _2, b2
  // RGBLed rgbled_5: pin names not known; wires that end beside it: r5, _5, b5
  // RGBLed rgbled_6: pin names not known; wires that end beside it: r8, _8, b8
  Counter #(.width(4), .max('h8)) counter_2 (
    .Q(counter_2_q), .clk(clk));  // open: load, D, count, carry, clr, preset, down
  Button SCORRI (.out(clk));
  // RGBLed rgbled_7: pin names not known; wires that end beside it: r3, _3, b3
  // RGBLed rgbled_8: pin names not known; wires that end beside it: r6, _6, b6
  // RGBLed rgbled_9: pin names not known; wires that end beside it: r9, _9, b9
  RAM #(.addrWidth(4), .dataWidth(2), .bus("separate"), .Select("low")) ram_1 (
    .addr(counter_2_q), .din(adder_1_out), .data(ram_1_data), .clk(out_1));  // open: str, sel, ld, clr
  and and_2 (out_1, CONFIRM_out, not_1_out[1], not_1_out[0]);
  assign not_1_out = ~ram_1_data;  // NOT_Gate not_1, 2 bits wide
  Demultiplexer #(.select(4), .width(2), .enable("false")) demultiplexer_1 (
    .out0(demultiplexer_1_out0), .out1(demultiplexer_1_out1), .out2(demultiplexer_1_out2),
    .out3(demultiplexer_1_out3), .out4(demultiplexer_1_out4), .out5(demultiplexer_1_out5),
    .out6(demultiplexer_1_out6), .out7(demultiplexer_1_out7), .out8(demultiplexer_1_out8), .in(ram_1_data),
    .sel(counter_2_q));  // open: out9, out10, out11, out12, out13, out14, out15
  Register #(.width(2), .trigger("falling"), .Select("low")) register_1 (
    .D(demultiplexer_1_out0), .en(_1), .Q({b1, r1}), .clk(clk));  // open: clr
  Decoder #(.select(4), .enable("false")) decoder_1 (
    .out0(_1), .out1(_2), .out2(_3), .out3(_4), .out4(_5), .out5(_6), .out6(_7), .out7(_8), .out8(_9),
    .sel(counter_2_q));  // open: out9, out10, out11, out12, out13, out14, out15
  Register #(.width(2), .trigger("falling"), .Select("low")) register_2 (
    .D(demultiplexer_1_out2), .en(_3), .Q({b3, r3}), .clk(clk));  // open: clr
  Register #(.width(2), .trigger("falling"), .Select("low")) register_3 (
    .D(demultiplexer_1_out4), .en(_5), .Q({b5, r5}), .clk(clk));  // open: clr
  Register #(.width(2), .trigger("falling"), .Select("low")) register_4 (
    .D(demultiplexer_1_out1), .en(_2), .Q({b2, r2}), .clk(clk));  // open: clr
  Register #(.width(2), .trigger("falling"), .Select("low")) register_5 (
    .D(demultiplexer_1_out6), .en(_7), .Q({b7, r7}), .clk(clk));  // open: clr
  Register #(.width(2), .trigger("falling"), .Select("low")) register_6 (
    .D(demultiplexer_1_out8), .en(_9), .Q({b9, r9}), .clk(clk));  // open: clr
  Register #(.width(2), .trigger("falling"), .Select("low")) register_7 (
    .D(demultiplexer_1_out3), .en(_4), .Q({b4, r4}), .clk(clk));  // open: clr
  Register #(.width(2), .trigger("falling"), .Select("low")) register_8 (
    .D(demultiplexer_1_out5), .en(_6), .Q({b6, r6}), .clk(clk));  // open: clr
  Register #(.width(2), .trigger("falling"), .Select("low")) register_9 (
    .D(demultiplexer_1_out7), .en(_8), .Q({b8, r8}), .clk(clk));  // open: clr
endmodule

module demux (
  input  CLK,
  input  _1,
  input  _2,
  input  _3,
  input  _4,
  input  _5,
  input  _6,
  input  _7,
  input  _8,
  input  [1:0] RAM_IN,
  input  _9,
  input  R1,
  input  B1,
  input  [3:0] ADDRESS_IN,
  input  R2,
  input  B2,
  input  R3,
  input  B3,
  input  R4,
  input  B4,
  input  R5,
  input  B5,
  input  B6,
  input  B6_2,
  input  R7,
  input  B7,
  input  R8,
  input  B8,
  input  R9,
  input  B9
);

  wire [1:0] demultiplexer_1_out0, demultiplexer_1_out1, demultiplexer_1_out2, demultiplexer_1_out3,
       demultiplexer_1_out4, demultiplexer_1_out5, demultiplexer_1_out6, demultiplexer_1_out7,
       demultiplexer_1_out8;

  Demultiplexer #(.select(4), .width(2), .enable("false")) demultiplexer_1 (
    .out0(demultiplexer_1_out0), .out1(demultiplexer_1_out1), .out2(demultiplexer_1_out2),
    .out3(demultiplexer_1_out3), .out4(demultiplexer_1_out4), .out5(demultiplexer_1_out5),
    .out6(demultiplexer_1_out6), .out7(demultiplexer_1_out7), .out8(demultiplexer_1_out8), .in(RAM_IN),
    .sel(ADDRESS_IN));  // open: out9, out10, out11, out12, out13, out14, out15
  Register #(.width(2), .trigger("falling"), .Select("low")) register_1 (
    .D(demultiplexer_1_out0), .en(_1), .Q({B1, R1}), .clk(CLK));  // open: clr
  Register #(.width(2), .trigger("falling"), .Select("low")) register_2 (
    .D(demultiplexer_1_out2), .en(_3), .Q({B3, R3}), .clk(CLK));  // open: clr
  Register #(.width(2), .trigger("falling"), .Select("low")) register_3 (
    .D(demultiplexer_1_out4), .en(_5), .Q({B5, R5}), .clk(CLK));  // open: clr
  Register #(.width(2), .trigger("falling"), .Select("low")) register_4 (
    .D(demultiplexer_1_out1), .en(_2), .Q({B2, R2}), .clk(CLK));  // open: clr
  Register #(.width(2), .trigger("falling"), .Select("low")) register_5 (
    .D(demultiplexer_1_out6), .en(_7), .Q({B7, R7}), .clk(CLK));  // open: clr
  Register #(.width(2), .trigger("falling"), .Select("low")) register_6 (
    .D(demultiplexer_1_out8), .en(_9), .Q({B9, R9}), .clk(CLK));  // open: clr
  Register #(.width(2), .trigger("falling"), .Select("low")) register_7 (
    .D(demultiplexer_1_out3), .en(_4), .Q({B4, R4}), .clk(CLK));  // open: clr
  Register #(.width(2), .trigger("falling"), .Select("low")) register_8 (
    .D(demultiplexer_1_out5), .en(_6), .Q({B6_2, B6}), .clk(CLK));  // open: clr
  Register #(.width(2), .trigger("falling"), .Select("low")) register_9 (
    .D(demultiplexer_1_out7), .en(_8), .Q({B8, R8}), .clk(CLK));  // open: clr

  // Other names for the same wires on the sheet: r6 = B6; b6_t = B6_2
endmodule

module decoder (
  input  [3:0] ADDRESS_IN,
  output _1,
  output _2,
  output _3,
  output _4,
  output _5,
  output _6,
  output _7,
  output _8,
  output _9
);

  Decoder #(.select(4), .enable("false")) decoder_1 (
    .out0(_1), .out1(_2), .out2(_3), .out3(_4), .out4(_5), .out5(_6), .out6(_7), .out7(_8), .out8(_9),
    .sel(ADDRESS_IN));  // open: out9, out10, out11, out12, out13, out14, out15
endmodule

module gestione_input (
  input  [1:0] DATA_OUT,
  input  CONFIRM,
  input  SCORRI,
  output [3:0] ADDRESS_IN,
  output [1:0] DATA_IN,
  output CLOCK_IN,
  output CLOCK_OUT
);

  wire and_1_out;
  wire [1:0] counter_1_q, not_1_out;

  Counter #(.width(2), .max('h1)) counter_1 (
    .Q(counter_1_q), .clk(and_1_out));  // open: load, D, count, carry, clr, preset, down
  and and_1 (and_1_out, CLOCK_IN, CONFIRM);
  Adder #(.width(2)) adder_1 (.a(2'b01), .b(counter_1_q), .out(DATA_IN));  // open: cin, cout
  Counter #(.width(4), .max('h8)) counter_2 (
    .Q(ADDRESS_IN), .clk(SCORRI), .clr(CONFIRM));  // open: load, D, count, carry, preset, down
  and and_2 (CLOCK_IN, CONFIRM, not_1_out[1], not_1_out[0]);
  assign not_1_out = ~DATA_OUT;  // NOT_Gate not_1, 2 bits wide

  assign CLOCK_OUT = SCORRI;
endmodule

module sottocircuiti (
);

  wire CLK, Confirm_out, decoder_1__1, decoder_1__2, decoder_1__3, decoder_1__4, decoder_1__5, decoder_1__6,
       decoder_1__7, decoder_1__8, decoder_1__9, gestione_input_1_clock_in, Scorri_out;
  wire [1:0] gestione_input_1_data_in, ram_1_data;
  wire [3:0] add;

  Button Scorri (.out(Scorri_out));
  Button Confirm (.out(Confirm_out));
  gestione_input gestione_input_1 (
    .DATA_IN(gestione_input_1_data_in), .ADDRESS_IN(add), .CLOCK_IN(gestione_input_1_clock_in),
    .DATA_OUT(ram_1_data), .CONFIRM(Confirm_out), .SCORRI(Scorri_out), .CLOCK_OUT(CLK));
  RAM #(.addrWidth(4), .dataWidth(2), .bus("separate"), .Select("low")) ram_1 (
    .addr(add), .din(gestione_input_1_data_in), .data(ram_1_data), .clk(gestione_input_1_clock_in));  // open: str, sel, ld, clr
  decoder decoder_1 (
    ._1(decoder_1__1), ._2(decoder_1__2), ._3(decoder_1__3), ._4(decoder_1__4), ._5(decoder_1__5),
    ._6(decoder_1__6), ._7(decoder_1__7), ._8(decoder_1__8), ._9(decoder_1__9), .ADDRESS_IN(add));
  demux demux_1 (
    .CLK(CLK), ._1(decoder_1__1), ._2(decoder_1__2), ._3(decoder_1__3), ._4(decoder_1__4), ._5(decoder_1__5),
    ._6(decoder_1__6), ._7(decoder_1__7), ._8(decoder_1__8), .RAM_IN(ram_1_data), ._9(decoder_1__9),
    .ADDRESS_IN(add));  // open: R1, B1, R2, B2, R3, B3, R4, B4, R5, B5, B6, B6_2, R7, B7, R8, B8, R9, B9
endmodule

module betino (
  output [1:0] out_1,
  output [1:0] out_2
);

  wire _1, _2, _3, _4, _5, _6, _7, _8, _9, ADD0, ADD1, ADD2, ADD3, ADD4, ADD5, ADD6, ADD8, and_1_out, b1, b2,
       b3, b4, b5, b6, b7, b8, b9, CLK, IOREQ, MREAD, MREQ, not_1_out, not_2_out, r1, r2, r3, r4, r5, r6, r7,
       r8, r9, RD, READ, RESET_out, SEL, WR, WRITE;
  wire [0:0] SCORRI_out;
  wire [1:0] ram_1_data;
  wire [6:0] ADDR;
  wire [7:0] DATAIN, multiplexer_1_out, rom_1_data;
  wire [7:2] \ß2018_1_p10 ;

  Button SCORRI (.out(SCORRI_out[0]));
  Controlled_Inverter #(.width(8)) controlled_inverter_1 (
    .in({{7{1'b0}}, SCORRI_out[0]}), .en(and_1_out));  // open: out
  and and_1 (and_1_out, ADD0, RD);
  not not_1 (not_1_out, SEL);
  not not_2 (not_2_out, CLK);
  RAM #(.addrWidth(7), .dataWidth(2), .bus("separate"), .Select("low")) ram_1 (
    .addr(ADDR), .din(out_1), .data(ram_1_data), .sel(not_1_out), .clk(not_2_out));  // open: str, ld, clr
  ROM #(.addrWidth(7), .Select("low")) rom_1 (.addr(ADDR), .data(rom_1_data), .sel(SEL));
  nor nor_1 (READ, RD, IOREQ);
  nor nor_2 (WRITE, WR, IOREQ);
  nor nor_3 (MREAD, RD, MREQ);
  Clock clock_1 (.out(CLK));
  Multiplexer #(.width(8), .enable("false")) multiplexer_1 (
    .in0(rom_1_data), .in1({{6{1'b0}}, ram_1_data}), .out(multiplexer_1_out), .sel(SEL));
  assign DATAIN = ~MREQ ? multiplexer_1_out : 8'bz;  // Controlled_Buffer controlled_buffer_1
  Button RESET (.out(RESET_out));
  // ß2018 ß2018_1: pin names not known; wires that end beside it: DATAIN, CLK, 1'b1, RESET_out, {SEL, ADDR}, MREQ, RD, IOREQ, WR, {\ß2018_1_p10 , out_1}
  // RGBLed rgbled_1: pin names not known; wires that end beside it: r1, _1, b1
  // RGBLed rgbled_2: pin names not known; wires that end beside it: r4, _4, b4
  // RGBLed rgbled_3: pin names not known; wires that end beside it: r7, _7, b7
  // RGBLed rgbled_4: pin names not known; wires that end beside it: r2, _2, b2
  // RGBLed rgbled_5: pin names not known; wires that end beside it: r5, _5, b5
  // RGBLed rgbled_6: pin names not known; wires that end beside it: r8, _8, b8
  // RGBLed rgbled_7: pin names not known; wires that end beside it: r3, _3, b3
  // RGBLed rgbled_8: pin names not known; wires that end beside it: r6, _6, b6
  // RGBLed rgbled_9: pin names not known; wires that end beside it: r9, _9, b9
  Decoder #(.select(3), .enable("false")) decoder_1 (
    .out0(ADD0), .out1(ADD1), .out2(ADD2), .out3(ADD3), .out4(ADD4), .out5(ADD5), .out6(ADD6), .out7(ADD8),
    .sel(ADDR[2:0]));
  decoder decoder_2 (
    ._1(_1), ._2(_2), ._3(_3), ._4(_4), ._5(_5), ._6(_6), ._7(_7), ._8(_8), ._9(_9), .ADDRESS_IN(ADDR[3:0]));
  demux demux_1 (
    .CLK(CLK), ._1(_1), ._2(_2), ._3(_3), ._4(_4), ._5(_5), ._6(_6), ._7(_7), ._8(_8), .RAM_IN(out_1),
    ._9(_9), .R1(r1), .B1(b1), .R2(r2), .B2(b2), .R3(r3), .B3(b3), .R4(r4), .B4(b4), .R5(r5), .B5(b5),
    .B6(r6), .B6_2(b6), .R7(r7), .B7(b7), .R8(r8), .B8(b8), .R9(r9), .B9(b9), .ADDRESS_IN(ADDR[3:0]));

  assign out_2 = out_1;

  // Other names for the same wires on the sheet: DATA[1:0] = out_1; ADDRLSB[3:0] = ADDR[3:0]

  // Notes on the sheet:
  //   SKINNY SEI ANCORA FATTO
  //   contents of rom_1 (hex, n*v repeats v):
  //   3e 1 32 81 76
endmodule

module prova (
  input  [6:0] in_1,
  input  [1:0] in_2,
  input  in_3,
  input  in_4,
  output [1:0] out_5
);

  wire not_1_out, not_2_out;

  not not_1 (not_1_out, in_3);
  not not_2 (not_2_out, in_4);
  RAM #(.addrWidth(7), .dataWidth(2), .bus("separate"), .Select("low")) ram_1 (
    .addr(in_1), .din(in_2), .sel(not_1_out), .clk(not_2_out));  // open: data, str, ld, clr

  assign out_5 = in_2;

  // Other names for the same wires on the sheet: ADDR[6:0] = in_1; CLK = in_4; DATA[1:0] = in_2; SEL = in_3
endmodule
